// Logisim project CN262 final project.circ as structural Verilog: 3 circuits, main circuit main
module main (
  input  startstop
);

  wire counter_1_carry, counter_2_carry, demultiplexer_1_out1, demultiplexer_1_out2, demultiplexer_1_out3,
       demultiplexer_2_out1, demultiplexer_2_out2, demultiplexer_2_out3, lap_out, or_1_out, reset_out,
       split_out;
  wire [1:0] counter_1_q, counter_2_q;
  wire [3:0] split_2_outhr01, split_2_outhr10, split_2_outmin01, split_2_outmin10, split_2_outsec01,
       split_2_outsec10, split_3_outhr01, split_3_outhr10, split_3_outmin01, split_3_outmin10,
       split_3_outsec01, split_3_outsec10, split_4_outhr01, split_4_outhr10, split_4_outmin01,
       split_4_outmin10, split_4_outsec01, split_4_outsec10, split_5_outhr01, split_5_outhr10,
       split_5_outmin01, split_5_outmin10, split_5_outsec01, split_5_outsec10, split_6_outhr01,
       split_6_outhr10, split_6_outmin01, split_6_outmin10, split_6_outsec01, split_6_outsec10,
       split_7_outhr01, split_7_outhr10, split_7_outmin01, split_7_outmin10, split_7_outsec01,
       split_7_outsec10, timer_1_hour01, timer_1_hour10, timer_1_minute01, timer_1_minute10, timer_1_sec01,
       timer_1_sec10, timer_2_hour01, timer_2_hour10, timer_2_minute01, timer_2_minute10, timer_2_sec01,
       timer_2_sec10;

  Button reset (.out(reset_out));
  Button split (.out(split_out));
  Button lap (.out(lap_out));
  Demultiplexer #(.select(2)) demultiplexer_1 (
    .out1(demultiplexer_1_out1), .out2(demultiplexer_1_out2), .out3(demultiplexer_1_out3), .in(1'b1),
    .sel(counter_1_q));  // open: out0, en
  Counter #(.width(2), .max('h3)) counter_1 (
    .Q(counter_1_q), .carry(counter_1_carry), .clk(split_out), .clr(counter_1_carry));  // open: load, D, count
  or or_1 (or_1_out, reset_out, lap_out);
  Demultiplexer #(.select(2)) demultiplexer_2 (
    .out1(demultiplexer_2_out1), .out2(demultiplexer_2_out2), .out3(demultiplexer_2_out3), .in(1'b1),
    .sel(counter_2_q));  // open: out0, en
  Counter #(.width(2), .max('h3)) counter_2 (
    .Q(counter_2_q), .carry(counter_2_carry), .clk(lap_out), .clr(counter_2_carry));  // open: load, D, count
  timer timer_1 (
    .startstop(startstop), .reset(reset_out), .sec01(timer_1_sec01), .sec10(timer_1_sec10),
    .minute01(timer_1_minute01), .minute10(timer_1_minute10), .hour01(timer_1_hour01), .hour10(timer_1_hour10));
  timer timer_2 (
    .startstop(startstop), .reset(or_1_out), .sec01(timer_2_sec01), .sec10(timer_2_sec10),
    .minute01(timer_2_minute01), .minute10(timer_2_minute10), .hour01(timer_2_hour01), .hour10(timer_2_hour10));
  Hex_Digit_Display hex_digit_display_1 (.value(timer_1_hour10));  // open: dp
  split split_2 (
    .savetime(demultiplexer_1_out1), .reset(reset_out), .insec01(timer_1_sec01), .insec10(timer_1_sec10),
    .inmin01(timer_1_minute01), .inmin10(timer_1_minute10), .inhr01(timer_1_hour01), .inhr10(timer_1_hour10),
    .outsec01(split_2_outsec01), .outsec10(split_2_outsec10), .outmin01(split_2_outmin01),
    .outmin10(split_2_outmin10), .outhr01(split_2_outhr01), .outhr10(split_2_outhr10));
  split split_3 (
    .savetime(demultiplexer_1_out2), .reset(reset_out), .insec01(timer_1_sec01), .insec10(timer_1_sec10),
    .inmin01(timer_1_minute01), .inmin10(timer_1_minute10), .inhr01(timer_1_hour01), .inhr10(timer_1_hour10),
    .outsec01(split_3_outsec01), .outsec10(split_3_outsec10), .outmin01(split_3_outmin01),
    .outmin10(split_3_outmin10), .outhr01(split_3_outhr01), .outhr10(split_3_outhr10));
  split split_4 (
    .savetime(demultiplexer_1_out3), .reset(reset_out), .insec01(timer_1_sec01), .insec10(timer_1_sec10),
    .inmin01(timer_1_minute01), .inmin10(timer_1_minute10), .inhr01(timer_1_hour01), .inhr10(timer_1_hour10),
    .outsec01(split_4_outsec01), .outsec10(split_4_outsec10), .outmin01(split_4_outmin01),
    .outmin10(split_4_outmin10), .outhr01(split_4_outhr01), .outhr10(split_4_outhr10));
  split split_5 (
    .savetime(demultiplexer_2_out1), .reset(reset_out), .insec01(timer_2_sec01), .insec10(timer_2_sec10),
    .inmin01(timer_2_minute01), .inmin10(timer_2_minute10), .inhr01(timer_2_hour01), .inhr10(timer_2_hour10),
    .outsec01(split_5_outsec01), .outsec10(split_5_outsec10), .outmin01(split_5_outmin01),
    .outmin10(split_5_outmin10), .outhr01(split_5_outhr01), .outhr10(split_5_outhr10));
  split split_6 (
    .savetime(demultiplexer_2_out2), .reset(reset_out), .insec01(timer_2_sec01), .insec10(timer_2_sec10),
    .inmin01(timer_2_minute01), .inmin10(timer_2_minute10), .inhr01(timer_2_hour01), .inhr10(timer_2_hour10),
    .outsec01(split_6_outsec01), .outsec10(split_6_outsec10), .outmin01(split_6_outmin01),
    .outmin10(split_6_outmin10), .outhr01(split_6_outhr01), .outhr10(split_6_outhr10));
  split split_7 (
    .savetime(demultiplexer_2_out3), .reset(reset_out), .insec01(timer_2_sec01), .insec10(timer_2_sec10),
    .inmin01(timer_2_minute01), .inmin10(timer_2_minute10), .inhr01(timer_2_hour01), .inhr10(timer_2_hour10),
    .outsec01(split_7_outsec01), .outsec10(split_7_outsec10), .outmin01(split_7_outmin01),
    .outmin10(split_7_outmin10), .outhr01(split_7_outhr01), .outhr10(split_7_outhr10));
  Hex_Digit_Display hex_digit_display_2 (.value(timer_1_hour01));  // open: dp
  Hex_Digit_Display hex_digit_display_3 (.value(split_2_outhr10));  // open: dp
  Hex_Digit_Display hex_digit_display_4 (.value(split_3_outhr10));  // open: dp
  Hex_Digit_Display hex_digit_display_5 (.value(split_4_outhr10));  // open: dp
  Hex_Digit_Display hex_digit_display_6 (.value(split_5_outhr10));  // open: dp
  Hex_Digit_Display hex_digit_display_7 (.value(split_6_outhr10));  // open: dp
  Hex_Digit_Display hex_digit_display_8 (.value(split_7_outhr10));  // open: dp
  Hex_Digit_Display hex_digit_display_9 (.value(timer_1_minute10));  // open: dp
  Hex_Digit_Display hex_digit_display_10 (.value(timer_1_minute01));  // open: dp
  Hex_Digit_Display hex_digit_display_11 (.value(split_2_outmin10));  // open: dp
  Hex_Digit_Display hex_digit_display_12 (.value(split_2_outhr01));  // open: dp
  Hex_Digit_Display hex_digit_display_13 (.value(split_3_outhr01));  // open: dp
  Hex_Digit_Display hex_digit_display_14 (.value(split_3_outmin10));  // open: dp
  Hex_Digit_Display hex_digit_display_15 (.value(split_4_outhr01));  // open: dp
  Hex_Digit_Display hex_digit_display_16 (.value(split_4_outmin10));  // open: dp
  Hex_Digit_Display hex_digit_display_17 (.value(split_5_outhr01));  // open: dp
  Hex_Digit_Display hex_digit_display_18 (.value(split_5_outmin10));  // open: dp
  Hex_Digit_Display hex_digit_display_19 (.value(split_6_outhr01));  // open: dp
  Hex_Digit_Display hex_digit_display_20 (.value(split_6_outmin10));  // open: dp
  Hex_Digit_Display hex_digit_display_21 (.value(split_7_outhr01));  // open: dp
  Hex_Digit_Display hex_digit_display_22 (.value(split_7_outmin10));  // open: dp
  Hex_Digit_Display hex_digit_display_23 (.value(timer_1_sec10));  // open: dp
  Hex_Digit_Display hex_digit_display_24 (.value(timer_1_sec01));  // open: dp
  Hex_Digit_Display hex_digit_display_25 (.value(split_2_outmin01));  // open: dp
  Hex_Digit_Display hex_digit_display_26 (.value(split_3_outmin01));  // open: dp
  Hex_Digit_Display hex_digit_display_27 (.value(split_4_outmin01));  // open: dp
  Hex_Digit_Display hex_digit_display_28 (.value(split_5_outmin01));  // open: dp
  Hex_Digit_Display hex_digit_display_29 (.value(split_6_outmin01));  // open: dp
  Hex_Digit_Display hex_digit_display_30 (.value(split_7_outmin01));  // open: dp
  Hex_Digit_Display hex_digit_display_31 (.value(split_2_outsec10));  // open: dp
  Hex_Digit_Display hex_digit_display_32 (.value(split_2_outsec01));  // open: dp
  Hex_Digit_Display hex_digit_display_33 (.value(split_3_outsec10));  // open: dp
  Hex_Digit_Display hex_digit_display_34 (.value(split_3_outsec01));  // open: dp
  Hex_Digit_Display hex_digit_display_35 (.value(split_4_outsec01));  // open: dp
  Hex_Digit_Display hex_digit_display_36 (.value(split_4_outsec10));  // open: dp
  Hex_Digit_Display hex_digit_display_37 (.value(split_5_outsec01));  // open: dp
  Hex_Digit_Display hex_digit_display_38 (.value(split_5_outsec10));  // open: dp
  Hex_Digit_Display hex_digit_display_39 (.value(split_6_outsec01));  // open: dp
  Hex_Digit_Display hex_digit_display_40 (.value(split_6_outsec10));  // open: dp
  Hex_Digit_Display hex_digit_display_41 (.value(split_7_outsec01));  // open: dp
  Hex_Digit_Display hex_digit_display_42 (.value(split_7_outsec10));  // open: dp

  // Notes on the sheet:
  //   Split1
  //   Split2
  //   Split3
  //   Lap1
  //   Lap2
  //   Lap3
endmodule

module timer (
  input  startstop,
  input  reset,
  output [3:0] sec01,
  output [3:0] sec10,
  output [3:0] minute01,
  output [3:0] minute10,
  output [3:0] hour01,
  output [3:0] hour10
);

  wire and_1_out, clock_1_out, counter_1_carry, counter_2_carry, counter_3_carry, counter_4_carry,
       counter_5_carry, counter_6_carry, or_1_out, or_2_out, or_3_out, or_4_out, or_5_out, or_6_out;

  and and_1 (and_1_out, startstop, clock_1_out);
  Clock clock_1 (.out(clock_1_out));
  Counter #(.width(4), .max('ha)) counter_1 (
    .Q(sec01), .carry(counter_1_carry), .clk(and_1_out), .clr(or_1_out));  // open: load, D, count
  or or_1 (or_1_out, reset, counter_1_carry);
  Counter #(.width(4), .max('h6)) counter_2 (
    .Q(sec10), .carry(counter_2_carry), .clk(counter_1_carry), .clr(or_2_out));  // open: load, D, count
  or or_2 (or_2_out, reset, counter_2_carry);
  Counter #(.width(4), .max('ha)) counter_3 (
    .Q(minute01), .carry(counter_3_carry), .clk(counter_2_carry), .clr(or_3_out));  // open: load, D, count
  or or_3 (or_3_out, reset, counter_3_carry);
  Counter #(.width(4), .max('h6)) counter_4 (
    .Q(minute10), .carry(counter_4_carry), .clk(counter_3_carry), .clr(or_4_out));  // open: load, D, count
  or or_4 (or_4_out, reset, counter_4_carry);
  Counter #(.width(4), .max('h9)) counter_5 (
    .Q(hour01), .carry(counter_5_carry), .clk(counter_4_carry), .clr(or_5_out));  // open: load, D, count
  or or_5 (or_5_out, reset, counter_5_carry);
  Counter #(.width(4), .max('h9)) counter_6 (
    .Q(hour10), .carry(counter_6_carry), .clk(counter_5_carry), .clr(or_6_out));  // open: load, D, count
  or or_6 (or_6_out, reset, counter_6_carry);
endmodule

module split (
  input  savetime,
  input  reset,
  input  [3:0] insec01,
  input  [3:0] insec10,
  input  [3:0] inmin01,
  input  [3:0] inmin10,
  input  [3:0] inhr01,
  input  [3:0] inhr10,
  output [3:0] outsec01,
  output [3:0] outsec10,
  output [3:0] outmin01,
  output [3:0] outmin10,
  output [3:0] outhr01,
  output [3:0] outhr10
);

  Register #(.width(4)) register_1 (.D(insec01), .Q(outsec01), .clk(savetime), .clr(reset));  // open: en
  Register #(.width(4)) register_2 (.D(insec10), .Q(outsec10), .clk(savetime), .clr(reset));  // open: en
  Register #(.width(4)) register_3 (.D(inmin01), .Q(outmin01), .clk(savetime), .clr(reset));  // open: en
  Register #(.width(4)) register_4 (.D(inmin10), .Q(outmin10), .clk(savetime), .clr(reset));  // open: en
  Register #(.width(4)) register_5 (.D(inhr01), .Q(outhr01), .clk(savetime), .clr(reset));  // open: en
  Register #(.width(4)) register_6 (.D(inhr10), .Q(outhr10), .clk(savetime), .clr(reset));  // open: en
endmodule
